# Fritzing sketch Attiny85 (saved by Fritzing 0.9.3b)
breadboards: 1

parts:
  U1 = attiny85 [package=dip]
  Part4 = LCD1602-I2C
  DS3 = DS18B20 1-Wire Temperature Sensor [part_number=DS18B20]
  U2 = LIPO-110mAh [package=lipo-110]

nets:
  N1: U1.Pin_2, DS3.DQ
  GND: U1.Pin_4, Part4.GND, DS3.GND, U2.-
  N2: U1.Pin_5, Part4.SDA
  N3: U1.Pin_7, Part4.SCL
  VCC: U1.Pin_8, Part4.VCC, DS3.VDD, U2.+

custom parts:
  LCD1602-I2C: A standard character display, usually with 2x16 characters. Comes in many colors with LCM1602 IIC attached.
